# Fritzing sketch ADS1115 module (saved by Fritzing 0.9.3b)
breadboards: 1

parts:
  Raspberry_Pi_1 = Raspberry Pi 3 [part_number=RPI-3-V1.2]
  Componente1 = Adafruit ADS1115 16Bit I2C ADC [part_number="Adafruit #1085"]

nets:
  N1: Raspberry_Pi_1.GPIO3, Componente1.SCL
  N2: Raspberry_Pi_1.GIPO4, Componente1.SDA
  3V3: Raspberry_Pi_1.3V3, Componente1.VDD
  GND: Raspberry_Pi_1.GND, Componente1.ADDR, Componente1.GND

custom parts:
  Adafruit ADS1115 16Bit I2C ADC: For microcontrollers without an analog-to-digital converter or when you want a higher-precision ADC, the ADS1115 provides 16-bit precision at 860 samples/second over I2C. The chip can be configured as 4 single-ended input channels, or two differential channels. As a nice bonus, it even includes a programmable gain amplifier, up to x16, to help boost up smaller single/differential signals to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
