# Fritzing sketch DHT11 Sensor (saved by Fritzing 0.9.3b)
breadboards: 1

parts:
  Raspberry_Pi_1 = Raspberry Pi 3 [part_number=RPI-3-V1.2]
  DHT11_1 = DHT11 module

nets:
  N1: Raspberry_Pi_1.3v3, DHT11_1.DATA
  N2: Raspberry_Pi_1.GIPO4, DHT11_1.VCC
  GND: Raspberry_Pi_1.GND, DHT11_1.GND

custom parts:
  DHT11 module: DHT11 black pcb module
